# Fritzing sketch TeensyHCSR04 (saved by Fritzing 0.9.6b)
circuit board: 4cm x 5cm
breadboards: 1

parts:
  Teensy_3_2 = Teensy 3.1
  10k_R = Resistor [tolerance=±5% power=0.25 resistance=220 package=THT]
  10k = Resistor [tolerance=±5% power=0.25 resistance=220 package=THT]
  HC-SR04 = HC-SR04 Ultrasonic Distance Sensor

nets:
  N1: Teensy_3_2.GND, 10k_R.Pin_0
  N2: Teensy_3_2.D0, HC-SR04.TRIG
  N3: Teensy_3_2.D1, 10k.Pin_0
  VIN: Teensy_3_2.Vin, HC-SR04.VCC
  N4: 10k_R.Pin_1, HC-SR04.GND
  N5: 10k.Pin_1, HC-SR04.ECHO

notes:
  vcc
  trig
  echo
  gnd
