# Fritzing sketch audioJackTeensy (saved by Fritzing 0.9.6b)
circuit board: 4.60891cm x 5.48857cm
breadboards: 1

parts:
  J1 = 3.5mm Audio Jack-mj-3523-smt.fzpz [package=audio-jack-3.5mm-smd]
  J2 = 3.5mm Audio Jack-mj-3523-smt.fzpz [package=audio-jack-3.5mm-smd]
  Teensy_3_1 = Teensy 3.1
  J3 = 3.5mm Audio Jack-mj-3523-smt.fzpz [package=audio-jack-3.5mm-smd]
  J4 = 3.5mm Audio Jack-mj-3523-smt.fzpz [package=audio-jack-3.5mm-smd]

nets:
  N1: J1.pin_1, J2.pin_1, Teensy_3_1.AGND, J3.pin_1, J4.pin_1
  N2: J1.Pin_2, Teensy_3_1.A9/D23
  N3: J2.Pin_2, Teensy_3_1.A8/D22
  N4: Teensy_3_1.A6/D20, J3.Pin_2
  N5: Teensy_3_1.A7/D21, J4.Pin_2

custom parts:
  3.5mm Audio Jack-mj-3523-smt.fzpz: 3.5mm Audio Jack MJ-3523-SMT 3.5mm mono jack.
